// Logisim project all_problem.circ as structural Verilog
module main (
  input  in_1,
  input  in_2,
  input  in_3,
  input  in_4,
  input  [2:0] in_5,
  input  in_6,
  input  in_7,
  input  in_8,
  input  in_9,
  input  in_10,
  input  in_11,
  input  in_12,
  input  in_13,
  input  [2:0] in_14,
  input  [24:0] in_15,
  input  in_16,
  input  [12:0] in_17,
  output out_18,
  output out_19,
  output [6:0] out_20,
  output out_21,
  output out_22,
  output [6:0] out_23
);

  prob2 prob2_1 (
    .a(in_6), .b(in_7), .c(in_8), .d(in_9), .e(in_10), .f(in_11), .g(in_12), .h(in_13), .sel(in_14),
    .y(out_21));
  prob5 prob5_1 (.en(in_16), .vt(in_17), .display(out_23));
  prob1 prob1_1 (.a(in_1), .b(in_2), .c(in_3), .d(in_4), .out1(out_18), .out2(out_19));
  prob4 prob4_1 (.vt(in_15), .result(out_22));
  prob3 prob3_1 (.sel(in_5), .display(out_20));
endmodule

// VHDL entity prob1, as the project stores it:
library ieee;
use ieee.std_logic_1164.all;

entity prob1 is
    port (
        a, b, c, d : in std_logic;
        out1       : out std_logic;
        out2       : out std_logic
    );
end entity prob1;

architecture bhv of prob1 is
begin
    out1 <= a and b and c and d;
    out2 <= a or b or c or d;
end architecture bhv;

// VHDL entity prob2, as the project stores it:
library ieee;
use ieee.std_logic_1164.all;

entity prob2 is
    port (
        a, b, c, d, e, f, g, h : in std_logic;                   -- 입력 핀 8개
        sel                    : in std_logic_vector(2 downto 0); -- 선택 핀 3비트
        y                      : out std_logic                    -- 출력 핀 1개
    );
end entity prob2;

architecture bhv of prob2 is
begin
    process(a, b, c, d, e, f, g, h, sel)
    begin
        case sel is
            when "000" => y <= a;
            when "001" => y <= b;
            when "010" => y <= c;
            when "011" => y <= d;
            when "100" => y <= e;
            when "101" => y <= f;
            when "110" => y <= g;
            when "111" => y <= h;
            when others => y <= '0';
        end case;
    end process;
end architecture bhv;

// VHDL entity prob3, as the project stores it:
library ieee;
use ieee.std_logic_1164.all;

entity prob3 is
    port (
        sel     : in std_logic_vector(2 downto 0);
        display : out std_logic_vector(6 downto 0) -- g f e d c b a 순서
    );
end entity prob3;

architecture bhv of prob3 is
begin
    process(sel)
    begin
        case sel is
            -- display: "g fedcba" (1: ON, 0: OFF)
            when "000" => display <= "1011111"; -- a
            when "001" => display <= "1111100"; -- b
            when "010" => display <= "0111001"; -- c
            when "011" => display <= "1011110"; -- d
            when "100" => display <= "1110001"; -- f
            when "101" => display <= "1101111"; -- g
            when others => display <= "0000000"; -- OFF
        end case;
    end process;
end architecture bhv;

// VHDL entity prob4, as the project stores it:
library ieee;
	use ieee.std_logic_1164.all;
	
	entity prob4 is
	    port (
	        vt     : in std_logic_vector(25 downto 1);
	        result : out std_logic
	    );
	end entity prob4;
	
	architecture bhv of prob4 is
	begin
	    process(vt)
	        variable sum : integer range 0 to 25;
	    begin
	        sum := 0;
	        for i in 1 to 25 loop
	            if vt(i) = '1' then
	                sum := sum + 1;
	            end if;
	        end loop;
	
	        if sum >= 13 then
	            result <= '1';
	        else
	            result <= '0';
	        end if;
	    end process;
	end architecture bhv;

// VHDL entity prob5, as the project stores it:
library ieee;
use ieee.std_logic_1164.all;

entity prob5 is
    port (
        en      : in std_logic;
        vt      : in std_logic_vector(13 downto 1);
        display : out std_logic_vector(6 downto 0) -- g f e d c b a
    );
end entity prob5;

architecture bhv of prob5 is
begin
    process(en, vt)
        variable sum : integer range 0 to 13;
    begin
        if en = '0' then
            display <= "0000000"; -- 소등 (OFF)
        else
            sum := 0;
            for i in 1 to 13 loop
                if vt(i) = '1' then
                    sum := sum + 1;
                end if;
            end loop;

            case sum is
                when 0 => display <= "0111111"; -- 0
                when 1 => display <= "0000110"; -- 1
                when 2 => display <= "1011011"; -- 2
                when 3 => display <= "1001111"; -- 3
                when 4 => display <= "1100110"; -- 4
                when 5 => display <= "1101101"; -- 5
                when 6 => display <= "1111101"; -- 6
                when 7 => display <= "0000111"; -- 7
                when 8 => display <= "1111111"; -- 8
                when 9 => display <= "1101111"; -- 9
                when 10 => display <= "1110111"; -- A
                when 11 => display <= "1111100"; -- b
                when 12 => display <= "0111001"; -- C
                when 13 => display <= "1011110"; -- d
                when others => display <= "0000000";
            end case;
        end if;
    end process;
end architecture bhv;
